// Logisim project Conversor de 7segmentos.circ as structural Verilog: 8 circuits, main circuit main
module main (
  input  in_1,
  input  in_2,
  input  in_3,
  output out_4,
  output out_5,
  output out_6,
  output out_7,
  output out_8,
  output out_9,
  output out_10
);

  Segmento_a segmento_a_1 (.E2(in_1), .E1(in_2), .E0(in_3), .a(out_4));
  Segmento_b segmento_b_1 (.E2(in_1), .E1(in_2), .E0(in_3), .b(out_5));
  Segmento_c segmento_c_1 (.E2(in_1), .E1(in_2), .E0(in_3), .c(out_6));
  Segmento_d segmento_d_1 (.E2(in_1), .E1(in_2), .E0(in_3), .d(out_7));
  Segmento_e segmento_e_1 (.E2(in_1), .E1(in_2), .E0(in_3), .e(out_8));
  Segmento_f segmento_f_1 (.E2(in_1), .E1(in_2), .E0(in_3), .f(out_9));
  Segmento_g segmento_g_1 (.E2(in_1), .E1(in_2), .E0(in_3), .g(out_10));
endmodule

module Segmento_a (
  input  E2,
  input  E1,
  input  E0,
  output a
);

  wire and_1_out, and_2_out, and_3_out, or_1_out;

  and and_1 (and_1_out, ~E2, E1, E1);  // AND_Gate
  and and_2 (and_2_out, E2, ~E1);  // AND_Gate
  and and_3 (and_3_out, E1, ~E0);  // AND_Gate
  or or_1 (or_1_out, and_1_out, and_2_out);
  or or_2 (a, or_1_out, and_3_out);
endmodule

module Segmento_b (
  input  E2,
  input  E1,
  input  E0,
  output b
);

  wire and_1_out, and_2_out, and_3_out, or_1_out;

  and and_1 (and_1_out, E2, ~E1);  // AND_Gate
  and and_2 (and_2_out, ~E1, ~E0);  // AND_Gate
  and and_3 (and_3_out, E2, ~E0);  // AND_Gate
  or or_1 (or_1_out, and_1_out, and_2_out);
  or or_2 (b, or_1_out, and_3_out);
endmodule

module Segmento_c (
  input  E2,
  input  E1,
  input  E0,
  output c
);

  wire and_1_out, and_2_out, or_1_out;

  and and_1 (and_1_out, E2, E0);
  and and_2 (and_2_out, ~E2, ~E0);  // AND_Gate
  or or_1 (or_1_out, and_1_out, and_2_out);
  or or_2 (c, or_1_out, E1);
endmodule

module Segmento_d (
  input  E2,
  input  E1,
  input  E0,
  output d
);

  wire and_1_out, and_2_out, or_1_out;

  and and_1 (and_1_out, E1, E0);
  and and_2 (and_2_out, ~E1, ~E0);  // AND_Gate
  or or_1 (or_1_out, and_1_out, and_2_out);
  or or_2 (d, ~E2, or_1_out);  // OR_Gate
endmodule

module Segmento_e (
  input  E2,
  input  E1,
  input  E0,
  output e
);

  wire and_1_out, and_2_out;

  and and_1 (and_1_out, ~E2, ~E0);  // AND_Gate
  and and_2 (and_2_out, E1, ~E0);  // AND_Gate
  or or_1 (e, and_1_out, and_2_out);
endmodule

module Segmento_f (
  input  E2,
  input  E1,
  input  E0,
  output f
);

  wire and_1_out, and_2_out, and_3_out, and_4_out;

  and and_1 (and_1_out, ~E2, ~E0);  // AND_Gate
  and and_2 (and_2_out, E1, ~E0);  // AND_Gate
  and and_3 (and_3_out, ~E2, E1);  // AND_Gate
  and and_4 (and_4_out, E2, ~E1, E0);  // AND_Gate
  or or_1 (f, and_1_out, and_2_out, and_3_out, and_4_out);
endmodule

module Segmento_g (
  input  E2,
  input  E1,
  input  E0,
  output g
);

  wire or_1_out;

  or or_1 (or_1_out, E2, ~E1);  // OR_Gate
  or or_2 (g, or_1_out, E0);
endmodule
