// Logisim project Registrador de 3bits.circ as structural Verilog: 1 circuit, main circuit main
module main (
  input  clock,
  input  In0,
  input  In1,
  input  In2,
  output Out0,
  output Out1,
  output Out2
);

  D_Flip_Flop d_ff_1 (.clk(clock), .D(In0), .Q(Out0));  // open: Qn, preset, en, reset
  D_Flip_Flop d_ff_2 (.clk(clock), .D(In1), .Q(Out1));  // open: Qn, preset, en, reset
  D_Flip_Flop d_ff_3 (.clk(clock), .D(In2), .Q(Out2));  // open: Qn, preset, en, reset
endmodule
