// Logisim project Somador de 3bits.circ as structural Verilog: 3 circuits, main circuit meio somador
module meio_somador (
  input  a,
  input  b,
  output s,
  output c0
);

  xor xor_1 (s, a, b);
  and and_1 (c0, a, b, b);
endmodule

module somador_completo (
  input  ci,
  input  a,
  input  b,
  output s,
  output c0
);

  wire meio_somador_1_c0, meio_somador_1_s, meio_somador_2_c0;

  meio_somador meio_somador_1 (.a(a), .b(b), .s(meio_somador_1_s), .c0(meio_somador_1_c0));
  meio_somador meio_somador_2 (.a(ci), .b(meio_somador_1_s), .s(s), .c0(meio_somador_2_c0));
  or or_1 (c0, meio_somador_2_c0, meio_somador_1_c0);
endmodule

module somador3bits (
  input  A0,
  input  A1,
  input  A2,
  input  B0,
  input  B1,
  input  B2,
  output S0,
  output S1,
  output S2,
  output carry
);

  wire meio_somador_1_c0, somador_completo_1_c0;

  meio_somador meio_somador_1 (.a(A0), .b(B0), .s(S0), .c0(meio_somador_1_c0));
  somador_completo somador_completo_1 (.ci(meio_somador_1_c0), .a(A1), .b(B1), .s(S1), .c0(somador_completo_1_c0));
  somador_completo somador_completo_2 (.ci(somador_completo_1_c0), .a(A2), .b(B2), .s(S2), .c0(carry));
endmodule
