// Logisim project projeto circuito somador síncrono  - erick vinicius justino da silva.circ as structural Verilog: 1 circuit, main circuit main
module main (
  input  A0,
  input  A1,
  input  A2,
  input  B0,
  input  B1,
  input  B2
);

  wire clock_out, main_1_out0, main_1_out1, main_1_out2, main_2_out_4, main_2_out_5, main_2_out_6,
       main_2_out_7, main_2_out_8, main_2_out_9, main_2_out_10, somador3bits_1_s0, somador3bits_1_s1,
       somador3bits_1_s2;

  Clock clock (.out(clock_out));
  somador3bits somador3bits_1 (
    .A0(A0), .A1(A1), .A2(A2), .B0(B0), .B1(B1), .B2(B2), .S0(somador3bits_1_s0), .S1(somador3bits_1_s1),
    .S2(somador3bits_1_s2));  // open: carry
  Registrador_de_3bits_main main_1 (
    .clock(clock_out), .In0(somador3bits_1_s2), .In1(somador3bits_1_s1), .In2(somador3bits_1_s0),
    .Out0(main_1_out0), .Out1(main_1_out1), .Out2(main_1_out2));
  Conversor_de_7segmentos_main main_2 (
    .in_1(main_1_out0), .in_2(main_1_out1), .in_3(main_1_out2), .out_4(main_2_out_4), .out_5(main_2_out_5),
    .out_6(main_2_out_6), .out_7(main_2_out_7), .out_8(main_2_out_8), .out_9(main_2_out_9),
    .out_10(main_2_out_10));
  _7_Segment_Display u_7_segment_display_1 (
    .g(main_2_out_4), .f(main_2_out_5), .a(main_2_out_6), .b(main_2_out_7), .e(main_2_out_8),
    .d(main_2_out_9), .c(main_2_out_10));  // open: dp

  // Notes on the sheet:
  //   Somador de 3 bits
  //   Registrador de 3 Bits
  //   Conversor de 7 segmentos
endmodule
